// Logisim project fib.circ as structural Verilog: 4 circuits, main circuit main
module main (
  input  [2:0] in_1,
  output [3:0] out_2
);

  wire count_1_res, not_1_out;
  wire [3:0] cal_1_output;

  count count_1 (.input_max(in_1), .res(count_1_res));  // open: in_2
  // Probe on cal_1_output
  Multiplexer #(.width(4)) multiplexer_1 (.in0(4'b0000), .in1(cal_1_output), .out(out_2), .sel(not_1_out));  // open: en
  cal cal_1 (.\output (cal_1_output), .en(count_1_res));
  not not_1 (not_1_out, count_1_res);
endmodule

module count (
  input  [2:0] input_max,
  input  in_2,
  output res
);

  wire clock_1_out;
  wire [7:0] bit_extender_1_out, counter_1_q;

  Clock clock_1 (.out(clock_1_out));
  assign bit_extender_1_out = {{5{1'b0}}, input_max};  // Bit_Extender bit_extender_1
  Counter counter_1 (.Q(counter_1_q), .clk(clock_1_out), .clr(in_2));  // open: load, D, count, carry
  Comparator #(.mode("unsigned")) comparator_1 (.a(bit_extender_1_out), .b(counter_1_q), .gt(res));  // open: eq, lt
endmodule

module cal (
  input  en,
  output [3:0] \output 
);

  wire clock;
  wire [3:0] adder_1_out, pre;

  reg_init reg_init_1 (.init(4'b0001), .D(\output ), .en(en), .clk(clock), .Q(pre));  // open: rst
  Adder #(.width(4)) adder_1 (.a(pre), .b(\output ), .out(adder_1_out));  // open: cin, cout
  Clock clock_1 (.out(clock));
  reg_init reg_init_2 (.init(4'b0000), .D(adder_1_out), .en(en), .clk(clock), .Q(\output ));  // open: rst

  // Other names for the same wires on the sheet: enable = en; now[3:0] = \output 
endmodule

module reg_init (
  input  [3:0] init,
  input  [3:0] D,
  input  en,
  input  clk,
  input  rst,
  output [3:0] Q
);

  wire counter_1_carry;
  wire [3:0] multiplexer_1_out, register_1_q;

  Pull_Resistor #(.pull(1)) pull_resistor_1 (.node(en));
  Multiplexer #(.width(4)) multiplexer_1 (.in0(Q), .in1(D), .out(multiplexer_1_out), .sel(en));  // open: en
  Pull_Resistor pull_resistor_2 (.node(init));
  Register #(.width(4)) register_1 (.D(multiplexer_1_out), .Q(register_1_q), .clk(clk), .clr(rst));  // open: en
  Counter #(.width(1), .max('h1), .ongoal("stay")) counter_1 (
    .carry(counter_1_carry), .clk(clk), .clr(rst));  // open: load, D, count, Q
  Multiplexer #(.width(4)) multiplexer_2 (.in0(init), .in1(register_1_q), .out(Q), .sel(counter_1_carry));  // open: en
endmodule
