// Logisim project register_with_initiation.circ as structural Verilog: 2 circuits, main circuit main
module reg_init (
  input  [31:0] init,
  input  [31:0] D,
  input  en,
  input  clk,
  input  rst,
  output [31:0] out_6
);

  wire counter_1_carry;
  wire [31:0] multiplexer_1_out, register_1_q;

  Pull_Resistor #(.pull(1)) pull_resistor_1 (.node(en));
  Multiplexer #(.width(32)) multiplexer_1 (.in0(out_6), .in1(D), .out(multiplexer_1_out), .sel(en));  // open: en
  Pull_Resistor pull_resistor_2 (.node(init));
  Register #(.width(32)) register_1 (.D(multiplexer_1_out), .Q(register_1_q), .clk(clk), .clr(rst));  // open: en
  Counter #(.width(1), .max('h1), .ongoal("stay")) counter_1 (
    .carry(counter_1_carry), .clk(clk), .clr(rst));  // open: load, D, count, Q
  Multiplexer #(.width(32)) multiplexer_2 (
    .in0(init), .in1(register_1_q), .out(out_6), .sel(counter_1_carry));  // open: en
endmodule

module main (
  input  [31:0] in_1,
  input  in_2,
  input  [31:0] in_3,
  output [31:0] out_4
);

  wire clock_1_out;

  Clock clock_1 (.out(clock_1_out));
  reg_init reg_init_1 (.init(in_1), .D(in_3), .en(1'b1), .clk(clock_1_out), .rst(in_2), .out_6(out_4));
endmodule
