// Logisim project fib_2.0.circ as structural Verilog: 6 circuits, main circuit main
module _0_1 (
  input  [31:0] \input ,
  output \end ,
  output state,
  output init
);

  wire clk, comparator_1_eq, init_t;
  wire [31:0] multiplexer_1_out, out, shifter_1_out;

  Clock clock_1 (.out(clk));
  Shifter #(.width(32), .shift("lr")) shifter_1 (.in(out), .\dist (5'b00001), .out(shifter_1_out));
  // Probe on out
  Register #(.width(32)) register_1 (.D(multiplexer_1_out), .Q(out), .clk(clk), .clr(init_t));  // open: en
  Multiplexer #(.width(32)) multiplexer_1 (
    .in0(\input ), .in1(shifter_1_out), .out(multiplexer_1_out), .sel(init));  // open: en
  Counter #(.width(1), .max('h1), .ongoal("stay")) counter_1 (.Q(init), .clk(clk));  // open: load, D, count, carry, clr
  Comparator #(.width(32), .mode("unsigned")) comparator_1 (
    .a(out), .b({32{1'b0}}), .eq(comparator_1_eq));  // open: gt, lt
  Multiplexer multiplexer_2 (.in0(1'b0), .in1(comparator_1_eq), .out(\end ), .sel(init));  // open: en
  Bit_Extender #(.in_width(32), .out_width(1)) bit_extender_1 (.in(out), .out(state));

  // Other names for the same wires on the sheet: sel = init
endmodule

module \矩阵乘法  (
  input  [31:0] a11,
  input  [31:0] a12,
  input  [31:0] a21,
  input  [31:0] a22,
  input  [31:0] b11,
  input  [31:0] b12,
  input  [31:0] b21,
  input  [31:0] b22,
  output [31:0] c11,
  output [31:0] c12,
  output [31:0] c21,
  output [31:0] c22
);

  wire [31:0] multiplier_1_out, multiplier_2_out, multiplier_3_out, multiplier_4_out, multiplier_5_out,
       multiplier_6_out, multiplier_7_out, multiplier_8_out;

  Multiplier #(.width(32)) multiplier_1 (.a(a11), .b(b12), .out(multiplier_1_out));  // open: cin, cout
  Multiplier #(.width(32)) multiplier_2 (.a(a12), .b(b22), .out(multiplier_2_out));  // open: cin, cout
  Multiplier #(.width(32)) multiplier_3 (.a(a21), .b(b11), .out(multiplier_3_out));  // open: cin, cout
  Multiplier #(.width(32)) multiplier_4 (.a(a22), .b(b21), .out(multiplier_4_out));  // open: cin, cout
  Multiplier #(.width(32)) multiplier_5 (.a(a21), .b(b12), .out(multiplier_5_out));  // open: cin, cout
  Multiplier #(.width(32)) multiplier_6 (.a(a22), .b(b22), .out(multiplier_6_out));  // open: cin, cout
  Multiplier #(.width(32)) multiplier_7 (.a(a11), .b(b11), .out(multiplier_7_out));  // open: cin, cout
  Adder #(.width(32)) adder_1 (.a(multiplier_7_out), .b(multiplier_8_out), .out(c11));  // open: cin, cout
  Multiplier #(.width(32)) multiplier_8 (.a(a12), .b(b21), .out(multiplier_8_out));  // open: cin, cout
  Adder #(.width(32)) adder_2 (.a(multiplier_1_out), .b(multiplier_2_out), .out(c12));  // open: cin, cout
  Adder #(.width(32)) adder_3 (.a(multiplier_3_out), .b(multiplier_4_out), .out(c21));  // open: cin, cout
  Adder #(.width(32)) adder_4 (.a(multiplier_5_out), .b(multiplier_6_out), .out(c22));  // open: cin, cout
endmodule

module main (
  input  [31:0] \input ,
  output [31:0] out_2
);

  wire clk, freeze, ini, not_1_out, not_2_out, state;
  wire [31:0] now_11, now_12, now_21, now_22, x11, x12, x21, x22, \初始化为对角阵_a11_2 , \初始化为对角阵_a12_2 ,
       \初始化为对角阵_a21_2 , \初始化为对角阵_a22_2 , \矩阵乘法_1_c11 , \矩阵乘法_1_c12 , \矩阵乘法_1_c21 , \矩阵乘法_1_c22 ,
       \矩阵乘法_2_c11 , \矩阵乘法_2_c12 , \矩阵乘法_2_c21 , \矩阵乘法_2_c22 , \矩阵选择器_对角阵_1_a11_2 , \矩阵选择器_对角阵_1_a12_2 ,
       \矩阵选择器_对角阵_1_a21_2 , \矩阵选择器_对角阵_1_a22_2 , \矩阵选择器_指数阵_1_a11_2 , \矩阵选择器_指数阵_1_a12_2 ,
       \矩阵选择器_指数阵_1_a21_2 , \矩阵选择器_指数阵_1_a22_2 ;

  Clock clock_1 (.out(clk));
  _0_1 u_0_1_1 (.\input (\input ), .\end (freeze), .state(state), .init(ini));
  \矩阵乘法  \u_矩阵乘法_1  (
    .a11(x11), .a12(x12), .a21(x21), .a22(x22), .b11(x11), .b12(x12), .b21(x21), .b22(x22),
    .c11(\矩阵乘法_1_c11 ), .c12(\矩阵乘法_1_c12 ), .c21(\矩阵乘法_1_c21 ), .c22(\矩阵乘法_1_c22 ));
  \矩阵选择器_对角阵  \u_矩阵选择器_对角阵_1  (
    .state(state), .a11(x11), .a12(x12), .a21(x21), .a22(x22), .a11_2(\矩阵选择器_对角阵_1_a11_2 ),
    .a12_2(\矩阵选择器_对角阵_1_a12_2 ), .a21_2(\矩阵选择器_对角阵_1_a21_2 ), .a22_2(\矩阵选择器_对角阵_1_a22_2 ));
  \reg  \u_矩阵寄存器  (
    .ena(not_1_out), .a11(\矩阵选择器_指数阵_1_a11_2 ), .a12(\矩阵选择器_指数阵_1_a12_2 ), .a21(\矩阵选择器_指数阵_1_a21_2 ),
    .a22(\矩阵选择器_指数阵_1_a22_2 ), .a11_2(x11), .a12_2(x12), .a21_2(x21), .a22_2(x22), .clk(clk));  // open: res
  \矩阵选择器_指数阵  \u_矩阵选择器_指数阵_1  (
    .state(ini), .a11(\矩阵乘法_1_c11 ), .a12(\矩阵乘法_1_c12 ), .a21(\矩阵乘法_1_c21 ), .a22(\矩阵乘法_1_c22 ),
    .a11_2(\矩阵选择器_指数阵_1_a11_2 ), .a12_2(\矩阵选择器_指数阵_1_a12_2 ), .a21_2(\矩阵选择器_指数阵_1_a21_2 ),
    .a22_2(\矩阵选择器_指数阵_1_a22_2 ));
  not not_1 (not_1_out, freeze);
  // Probe on now_12
  \矩阵乘法  \u_矩阵乘法_2  (
    .a11(now_11), .a12(now_12), .a21(now_21), .a22(now_22), .b11(\矩阵选择器_对角阵_1_a11_2 ),
    .b12(\矩阵选择器_对角阵_1_a12_2 ), .b21(\矩阵选择器_对角阵_1_a21_2 ), .b22(\矩阵选择器_对角阵_1_a22_2 ), .c11(\矩阵乘法_2_c11 ),
    .c12(\矩阵乘法_2_c12 ), .c21(\矩阵乘法_2_c21 ), .c22(\矩阵乘法_2_c22 ));
  \矩阵选择器_对角阵  \u_初始化为对角阵  (
    .state(ini), .a11(\矩阵乘法_2_c11 ), .a12(\矩阵乘法_2_c12 ), .a21(\矩阵乘法_2_c21 ), .a22(\矩阵乘法_2_c22 ),
    .a11_2(\初始化为对角阵_a11_2 ), .a12_2(\初始化为对角阵_a12_2 ), .a21_2(\初始化为对角阵_a21_2 ), .a22_2(\初始化为对角阵_a22_2 ));
  \reg  \u_矩阵寄存器_2  (
    .ena(not_2_out), .a11(\初始化为对角阵_a11_2 ), .a12(\初始化为对角阵_a12_2 ), .a21(\初始化为对角阵_a21_2 ),
    .a22(\初始化为对角阵_a22_2 ), .a11_2(now_11), .a12_2(now_12), .a21_2(now_21), .a22_2(now_22), .clk(clk));  // open: res
  not not_2 (not_2_out, freeze);
  Multiplexer #(.width(32)) multiplexer_1 (.in0({32{1'b0}}), .in1(now_12), .out(out_2), .sel(freeze));  // open: en
endmodule

module \矩阵选择器_对角阵  (
  input  state,
  input  [31:0] a11,
  input  [31:0] a12,
  input  [31:0] a21,
  input  [31:0] a22,
  output [31:0] a11_2,
  output [31:0] a12_2,
  output [31:0] a21_2,
  output [31:0] a22_2
);

  Multiplexer #(.width(32)) multiplexer_1 (.in0(32'h1), .in1(a11), .out(a11_2), .sel(state), .en(1'b1));
  Multiplexer #(.width(32)) multiplexer_2 (.in0({32{1'b0}}), .in1(a12), .out(a12_2), .sel(state), .en(1'b1));
  Multiplexer #(.width(32)) multiplexer_3 (.in0({32{1'b0}}), .in1(a21), .out(a21_2), .sel(state), .en(1'b1));
  Multiplexer #(.width(32)) multiplexer_4 (.in0(32'h1), .in1(a22), .out(a22_2), .sel(state), .en(1'b1));

  // Other names for the same wires on the sheet: states = state
endmodule

module \reg  (
  input  clk,
  input  res,
  input  ena,
  input  [31:0] a11,
  input  [31:0] a12,
  input  [31:0] a21,
  input  [31:0] a22,
  output [31:0] a11_2,
  output [31:0] a12_2,
  output [31:0] a21_2,
  output [31:0] a22_2
);

  Register #(.width(32)) register_1 (.D(a11), .en(ena), .Q(a11_2), .clk(clk), .clr(res));
  Register #(.width(32)) register_2 (.D(a12), .en(ena), .Q(a12_2), .clk(clk), .clr(res));
  Register #(.width(32)) register_3 (.D(a21), .en(ena), .Q(a21_2), .clk(clk), .clr(res));
  Register #(.width(32)) register_4 (.D(a22), .en(ena), .Q(a22_2), .clk(clk), .clr(res));
endmodule

module \矩阵选择器_指数阵  (
  input  state,
  input  [31:0] a11,
  input  [31:0] a12,
  input  [31:0] a21,
  input  [31:0] a22,
  output [31:0] a11_2,
  output [31:0] a12_2,
  output [31:0] a21_2,
  output [31:0] a22_2
);

  Multiplexer #(.width(32)) multiplexer_1 (.in0(32'h1), .in1(a11), .out(a11_2), .sel(state), .en(1'b1));
  Multiplexer #(.width(32)) multiplexer_2 (.in0(32'h1), .in1(a12), .out(a12_2), .sel(state), .en(1'b1));
  Multiplexer #(.width(32)) multiplexer_3 (.in0(32'h1), .in1(a21), .out(a21_2), .sel(state), .en(1'b1));
  Multiplexer #(.width(32)) multiplexer_4 (.in0({32{1'b0}}), .in1(a22), .out(a22_2), .sel(state), .en(1'b1));

  // Other names for the same wires on the sheet: states = state
endmodule
