// Logisim project mod5.circ as structural Verilog: 3 circuits, main circuit mod5
module mod5 (
  input  b,
  output S0,
  output S1,
  output S2,
  output S3,
  output S4
);

  wire clock_1_out;
  wire [1:0] register_1_q, \转移_1_c1_c0_ ;

  \转移  \u_转移_1  (.C1C0(register_1_q), .C1_C0_(\转移_1_c1_c0_ ), .b(b));
  Clock clock_1 (.out(clock_1_out));
  Register #(.width(2)) register_1 (.D(\转移_1_c1_c0_ ), .Q(register_1_q), .clk(clock_1_out));  // open: en, clr
  \输出状态  \u_输出状态_1  (.C1C0(register_1_q), .b(b), .S0(S0), .S1(S1), .S2(S2), .S3(S4), .S4(S3));
endmodule

module \转移  (
  input  b,
  input  [1:0] C1C0,
  output [1:0] C1_C0_
);


  assign C1_C0_ = {C1C0[0], b};
endmodule

module \输出状态  (
  input  [1:0] C1C0,
  input  b,
  output S0,
  output S1,
  output S2,
  output S3,
  output S4
);

  wire not_1_out, not_2_out, not_3_out, not_4_out;

  not not_1 (not_1_out, C1C0[0]);
  not not_2 (not_2_out, b);
  not not_3 (not_3_out, C1C0[0]);
  not not_4 (not_4_out, b);
  and and_1 (S4, C1C0[0], b);
  and and_2 (S1, not_1_out, not_2_out);
  and and_3 (S2, not_3_out, b);
  and and_4 (S3, C1C0[0], not_4_out);

  assign S0 = 1'b0;
endmodule
