// Logisim project sort.circ as structural Verilog: 5 circuits, main circuit main
module main (
  input  [3:0] in_1,
  input  [3:0] in_2,
  input  [3:0] in_3,
  input  [3:0] in_4,
  output [3:0] out_5,
  output [3:0] out_6,
  output [3:0] out_7,
  output [3:0] out_8
);

  _4bit_sort u_4bit_sort_1 (
    .I1(in_1), .I2(in_2), .I3(in_3), .I4(in_4), .out_5(out_8), .out_6(out_7), .out_7(out_6), .out_8(out_5));
endmodule

module _1bit_swap (
  input  I1,
  input  I2,
  input  S,
  output O1,
  output O2
);

  wire and_1_out, and_2_out, and_3_out, and_4_out, not_1_out, not_2_out;

  not not_1 (not_1_out, S);
  not not_2 (not_2_out, S);
  and and_1 (and_1_out, I1, not_1_out);
  and and_2 (and_2_out, I2, S);
  and and_3 (and_3_out, I1, S);
  and and_4 (and_4_out, I2, not_2_out);
  or or_1 (O1, and_1_out, and_2_out);
  or or_2 (O2, and_3_out, and_4_out);
endmodule

module _4bit_swap (
  input  in_1,
  input  [3:0] top,
  input  [3:0] bottom,
  output [3:0] after_bottom,
  output [3:0] after_top
);

  _1bit_swap _1 (.I1(top[0]), .I2(bottom[0]), .S(in_1), .O1(after_top[0]), .O2(after_bottom[0]));
  _1bit_swap _2 (.I1(top[1]), .I2(bottom[1]), .S(in_1), .O1(after_top[1]), .O2(after_bottom[1]));
  _1bit_swap _3 (.I1(top[2]), .I2(bottom[2]), .S(in_1), .O1(after_top[2]), .O2(after_bottom[2]));
  _1bit_swap _4 (.I1(top[3]), .I2(bottom[3]), .S(in_1), .O1(after_top[3]), .O2(after_bottom[3]));

  // Other names for the same wires on the sheet: _1_prime_1 = after_bottom[0]; _2_prime_2 = after_bottom[1];
  //   _3_prime_3 = after_bottom[2]; _4_prime_4 = after_bottom[3]; _1_prime = after_top[0]; _2_prime = after_top[1];
  //   _3_prime = after_top[2]; _4_prime = after_top[3]; _1_prime_prime = bottom[0]; _2_prime_prime = bottom[1];
  //   _3_prime_prime = bottom[2]; _4_prime_prime = bottom[3]; _1 = top[0]; _2 = top[1]; _3 = top[2]; _4 = top[3]
endmodule

module _4bit_sort (
  input  [3:0] I1,
  input  [3:0] I2,
  input  [3:0] I3,
  input  [3:0] I4,
  output [3:0] out_5,
  output [3:0] out_6,
  output [3:0] out_7,
  output [3:0] out_8
);

  wire [3:0] if_top_bottom_swap_1_after_bottom, if_top_bottom_swap_1_after_top,
       if_top_bottom_swap_2_after_bottom, if_top_bottom_swap_2_after_top, if_top_bottom_swap_3_after_top,
       if_top_bottom_swap_4_after_bottom, if_top_bottom_swap_4_after_top, if_top_bottom_swap_5_after_top;

  if_top_bottom_swap if_top_bottom_swap_1 (
    .top(I1), .bottom(I2), .after_top(if_top_bottom_swap_1_after_top),
    .after_bottom(if_top_bottom_swap_1_after_bottom));
  if_top_bottom_swap if_top_bottom_swap_2 (
    .top(if_top_bottom_swap_1_after_bottom), .bottom(I3), .after_top(if_top_bottom_swap_2_after_top),
    .after_bottom(if_top_bottom_swap_2_after_bottom));
  if_top_bottom_swap if_top_bottom_swap_3 (
    .top(if_top_bottom_swap_2_after_bottom), .bottom(I4), .after_top(if_top_bottom_swap_3_after_top),
    .after_bottom(out_8));
  if_top_bottom_swap if_top_bottom_swap_4 (
    .top(if_top_bottom_swap_1_after_top), .bottom(if_top_bottom_swap_2_after_top),
    .after_top(if_top_bottom_swap_4_after_top), .after_bottom(if_top_bottom_swap_4_after_bottom));
  if_top_bottom_swap if_top_bottom_swap_5 (
    .top(if_top_bottom_swap_4_after_bottom), .bottom(if_top_bottom_swap_3_after_top),
    .after_top(if_top_bottom_swap_5_after_top), .after_bottom(out_7));
  if_top_bottom_swap if_top_bottom_swap_6 (
    .top(if_top_bottom_swap_4_after_top), .bottom(if_top_bottom_swap_5_after_top), .after_top(out_5),
    .after_bottom(out_6));
endmodule

module if_top_bottom_swap (
  input  [3:0] top,
  input  [3:0] bottom,
  output [3:0] after_top,
  output [3:0] after_bottom
);

  wire comparator_1_lt;

  Comparator #(.width(4), .mode("unsigned")) comparator_1 (.a(top), .b(bottom), .lt(comparator_1_lt));  // open: gt, eq
  _4bit_swap u_4bit_swap_1 (
    .top(top), .bottom(bottom), .after_top(after_top), .after_bottom(after_bottom), .in_1(comparator_1_lt));
endmodule
